# Fritzing sketch freemcom (saved by Fritzing 0.8.5b)
breadboards: 1

parts:
  arduino = Arduino Uno (Rev3)
  Start/Stop = Pushbutton [package="[THT]"]
  R1 = Resistor [tolerance=±5% resistance=10k package=THT]
  LED1_(for_12V) = LED - 5mm [color="Red (633nm)" package="5 mm [THT]"]
  J1 = Relay [part_number=FRS1B-S package=THT]
  VCC2 = Battery
  VCC3 = Battery
  VCC4 = Battery
  VCC1 = Battery
  J2 = Relay [part_number=FRS1B-S package=THT]
  Buzzer(12V) = Piezo Speaker
  Reset = Pushbutton [package="[THT]"]

nets (from the schematic view):
  N1: arduino.GND, R1.Pin_1, J1.COIL1, J2.COIL1, Reset.Pin_1, Reset.Pin_2
  N2: arduino.D2, Start/Stop.Pin_1, Start/Stop.Pin_2, R1.Pin_0
  N3: arduino.D4, J1.COIL2
  N4: arduino.D5_PWM, J2.COIL2
  N5: arduino.RESET, Reset.Pin_3, Reset.Pin_4
  N6: arduino.5V, Start/Stop.Pin_3, Start/Stop.Pin_4
  N7: LED1_(for_12V).cathode, VCC4.-, Buzzer(12V).pin1
  N8: LED1_(for_12V).anode, J2.C1
  N9: J1.A, VCC1.+, J2.A
  N10: J1.C1, Buzzer(12V).pin2
  N11: VCC2.-, VCC3.+
  N12: VCC2.+, VCC1.-
  N13: VCC3.-, VCC4.+
